# Fritzing sketch human_IR-detected_light2 (saved by Fritzing 0.9.3b)
circuit board: 8.46667cm x 5.64444cm
breadboards: 1

parts:
  MCU = Arduino Nano (Rev3.0)
  K1 = Relay [part_number=FRS1B-S package=THT]
  LED1 = LED - 5mm [color="White (4500K)" package="5 mm [THT]"]  # not connected
  LED2 = LED - 5mm [color="White (4500K)" package="5 mm [THT]"]
  LED3 = LED - 5mm [color="White (4500K)" package="5 mm [THT]"]
  LED4 = LED - 5mm [color="White (4500K)" package="5 mm [THT]"]
  LED5 = LED - 5mm [color="White (4500K)" package="5 mm [THT]"]
  R1 = Resistor [tolerance=±5% resistance=220 package=THT]
  R2 = Resistor [tolerance=±5% resistance=220 package=THT]
  R3 = Resistor [tolerance=±5% resistance=220 package=THT]
  R4 = Resistor [tolerance=±5% resistance=220 package=THT]
  R5 = Resistor [tolerance=±5% resistance=220 package=THT]
  PIR1 = PIR sensor

nets:
  GND: MCU.GND, K1.COIL1, LED2.cathode, LED3.cathode, LED4.cathode, LED5.cathode, PIR1.GND
  N1: MCU.D2, K1.COIL2
  N2: MCU.D4, PIR1.SIG
  5V: MCU.5V, PIR1.VDD
  N3: K1.C1, K1.C2, R1.Pin_1, R2.Pin_1, R3.Pin_1, R4.Pin_1, R5.Pin_1

notes:
  NC
